# Fritzing sketch RGBakonexioak (saved by Fritzing 0.8.7b)
breadboards: 1

parts:
  LED1 = RGB LED (com. cathode, rgb) [package="5 mm [THT]"]
  R1 = Resistor [tolerance=±5% resistance=220 package=THT]
  R2 = Resistor [tolerance=±5% resistance=220 package=THT]
  R3 = Resistor [tolerance=±5% resistance=220 package=THT]
  Parte1 = iceZUM Alhambra

nets:
  N1: LED1.red_anode, LED1.green_anode, LED1.blue_anode, R1.Pin_0, R2.Pin_0, R3.Pin_0
  N2: LED1.common_cathode, Parte1.5V
  N3: R1.Pin_1, R2.Pin_1, R3.Pin_1, Parte1.D0, Parte1.D1, Parte1.D2, Parte1.V1, Parte1.V0
  N4: Parte1.DD1, Parte1.DD2, Parte1.DD3, Parte1.DD4, Parte1.DD5, Parte1.VD1, Parte1.VD2, Parte1.VD3, Parte1.VD4, Parte1.VD5, Parte1.GD1, Parte1.GD2, Parte1.GD3, Parte1.GD4, Parte1.GD5

notes:
  RGBaren 1.(gorria), 3.(berdea) eta 4. (urdina) borneei 220 Ohmeko erresistentzia konektatzen zaie seriean.
  RGBaren 2. bornea plakaren 5Vra konektatuko da

custom parts:
  iceZUM Alhambra: Arduino/zum compatible Open FPGA electronic board. Synthesize hardware easily, using only open source tools
