# Fritzing sketch 7 segmentuko display anodoa (saved by Fritzing 0.8.7b)
breadboards: 1

parts:
  7_Segment5 = 7 Segment Display
  Parte1 = Icezum Alhambra
  R1 = Resistor [tolerance=±5% resistance=220 package=THT]

nets:
  N1: 7_Segment5.Segment_E, Parte1.D5
  N2: 7_Segment5.Segment_D, Parte1.D6
  N3: 7_Segment5.common_cathode, R1.Pin_1
  N4: 7_Segment5.Segment_C, Parte1.D7
  N5: 7_Segment5.Segment_B, Parte1.D8
  N6: 7_Segment5.Segment_A, Parte1.D9
  N7: 7_Segment5.Segment_F, Parte1.D4
  N8: 7_Segment5.Segment_G, Parte1.D3
  N9: Parte1.3V3, R1.Pin_0

notes:
  Erresistentzia 330 edo 220 Ohm.

custom parts:
  Icezum Alhambra: The Arduino Uno is a microcontroller board based on the ATmega328 (datasheet). It has 14 digital input/output pins (of which 6 can be used as PWM outputs), 6 analog inputs, a 16 MHz ceramic resonator, a USB connection, a power jack, an ICSP header, and a reset button. It contains everything needed to support the microcontroller; simply connect it to a computer with a USB cable or power it with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
