# Fritzing sketch 7_segmentuko_display_anodoa (saved by Fritzing 0.9.3b)
breadboards: 1

parts:
  7_Segment1 = 7 Segment Display
  R11 = Resistor [tolerance=±5% resistance=220 package="0402 [SMD]"]
  R12 = Resistor [tolerance=±5% resistance=220 package="0402 [SMD]"]
  R13 = Resistor [tolerance=±5% resistance=220 package="0402 [SMD]"]
  R14 = Resistor [tolerance=±5% resistance=220 package="0402 [SMD]"]
  R15 = Resistor [tolerance=±5% resistance=220 package="0402 [SMD]"]
  R16 = Resistor [tolerance=±5% resistance=220 package="0402 [SMD]"]
  R17 = Resistor [tolerance=±5% resistance=220 package="0402 [SMD]"]
  Componente1 = iceZUM Alhambra

nets:
  N1: 7_Segment1.Segment_E, R13.Pin_1
  N2: 7_Segment1.Segment_D, R14.Pin_1
  N3: 7_Segment1.common_anode, Componente1.5VP
  N4: 7_Segment1.Segment_C, R15.Pin_1
  N5: 7_Segment1.Segment_B, R16.Pin_0
  N6: 7_Segment1.Segment_A, R17.Pin_0
  N7: 7_Segment1.Segment_F, R12.Pin_0
  N8: 7_Segment1.Segment_G, R11.Pin_0
  N9: R11.Pin_1, Componente1.D3, Componente1.V3
  N10: R12.Pin_1, Componente1.D4, Componente1.V4
  N11: R13.Pin_0, Componente1.D5, Componente1.V5
  N12: R14.Pin_0, Componente1.D6, Componente1.V6
  N13: R15.Pin_0, Componente1.D7, Componente1.V7
  N14: R16.Pin_1, Componente1.D8, Componente1.V8
  N15: R17.Pin_1, Componente1.D9

notes:
  R 330Ω

custom parts:
  iceZUM Alhambra: Arduino/zum compatible Open FPGA electronic board. Synthesize hardware easily, using only open source tools
