# Fritzing sketch 7seg-Katodo (saved by Fritzing 0.9.3b)
breadboards: 1

parts:
  Part1 = iceZUM Alhambra
  DI1 = 7-Segment LED Display [package=THT]
  R1 = Resistor [tolerance=±5% resistance=100 package=THT]
  R2 = Resistor [tolerance=±5% resistance=100 package=THT]
  R3 = Resistor [tolerance=±5% resistance=100 package=THT]
  R4 = Resistor [tolerance=±5% resistance=100 package=THT]
  R5 = Resistor [tolerance=±5% resistance=100 package=THT]
  R6 = Resistor [tolerance=±5% resistance=100 package=THT]
  R7 = Resistor [tolerance=±5% resistance=100 package=THT]
  R8 = Resistor [tolerance=±5% resistance=100 package=THT]

nets:
  N1: Part1.GD5, DI1.commAnode#7
  N2: Part1.GP0, R7.Pin_0
  N3: Part1.GP1, R8.Pin_0
  N4: Part1.GP2, R6.Pin_0
  N5: Part1.GP3, R5.Pin_0
  N6: Part1.GP4, R4.Pin_1
  N7: Part1.GP5, R1.Pin_1
  N8: Part1.GP6, R2.Pin_1
  N9: Part1.GP7, R3.Pin_1
  N10: DI1.cathodeE, R6.Pin_1
  N11: DI1.cathodeD, R5.Pin_1
  N12: DI1.cathodeC, R4.Pin_0
  N13: DI1.cathodeDP, R3.Pin_0
  N14: DI1.cathodeB, R1.Pin_0
  N15: DI1.cathodeA, R2.Pin_0
  N16: DI1.cathodeF, R8.Pin_1
  N17: DI1.cathodeG, R7.Pin_1

custom parts:
  iceZUM Alhambra: Arduino/zum compatible Open FPGA electronic board. Synthesize hardware easily, using only open source tools
