# Fritzing sketch Display4digAlhambra (saved by Fritzing 0.9.3b)
breadboards: 1

parts:
  Q1 = NPN-Transistor [package="TO92 [THT]"]
  R1 = Resistor [tolerance=±5% resistance=220 package=THT]
  R2 = Resistor [tolerance=±5% resistance=220 package=THT]
  R3 = Resistor [tolerance=±5% resistance=220 package=THT]
  R4 = Resistor [tolerance=±5% resistance=220 package=THT]
  R5 = Resistor [tolerance=±5% resistance=220 package=THT]
  R6 = Resistor [tolerance=±5% resistance=220 package=THT]
  R7 = Resistor [tolerance=±5% resistance=220 package=THT]
  LED1 = 7-SEGMENT-4DIGIT-YOUNGSUN [package=7-segment-4digit-youngsun-longpads]
  Parte1 = iceZUM Alhambra
  Q2 = NPN-Transistor [package="TO92 [THT]"]
  Q3 = NPN-Transistor [package="TO92 [THT]"]
  Q4 = NPN-Transistor [package="TO92 [THT]"]
  R8 = Resistor [tolerance=±5% resistance=220 package=THT]
  R9 = Resistor [tolerance=±5% resistance=220 package=THT]
  R10 = Resistor [tolerance=±5% resistance=220 package=THT]
  R11 = Resistor [tolerance=±5% resistance=220 package=THT]

nets:
  N1: Q1.E, Parte1.GND, Q2.E, Q3.E, Q4.E
  N2: Q1.B, R8.Pin_0
  N3: Q1.C, LED1.B
  N4: R1.Pin_0, Parte1.GP1
  N5: R1.Pin_1, LED1.F
  N6: R2.Pin_0, Parte1.GP5
  N7: R2.Pin_1, LED1.A
  N8: R3.Pin_0, Parte1.GP0
  N9: R3.Pin_1, LED1.G
  N10: R4.Pin_0, LED1.DIG1
  N11: R4.Pin_1, Parte1.GP4
  N12: R5.Pin_0, LED1.DIG2
  N13: R5.Pin_1, Parte1.GP3
  N14: R6.Pin_0, LED1.COL-A
  N15: R6.Pin_1, Parte1.GP2
  N16: R7.Pin_0, LED1.E
  N17: R7.Pin_1, Parte1.GP6
  N18: LED1.DIG3, Q4.C
  N19: LED1.COL-C, Q3.C
  N20: LED1.C, Q2.C
  N21: Parte1.D0, Parte1.V0, R11.Pin_1
  N22: Parte1.D1, Parte1.V1, R10.Pin_1
  N23: Parte1.D2, Parte1.V2, R9.Pin_1
  N24: Parte1.D3, Parte1.V3, R8.Pin_1
  N25: Q2.B, R9.Pin_0
  N26: Q3.B, R10.Pin_0
  N27: Q4.B, R11.Pin_0

notes:
  Transistoreen oinarrietan 1000 Ωeko erresistentziak konektatuko ditugu.
  Segmentuetara 330 Ωeko erresistentziak konektatuko ditugu.

custom parts:
  iceZUM Alhambra: Arduino/zum compatible Open FPGA electronic board. Synthesize hardware easily, using only open source tools
